// Digital circuit 74163-RD.dig as structural Verilog
module _74163_RD (
  input  nCLR,
  input  CLK,
  input  nLOAD,
  input  ENT,
  input  ENP,
  input  A,
  input  B,
  input  C,
  input  D,
  input  VCC,
  input  GND,
  output RC,
  output Q_A,
  output Q_B,
  output Q_C,
  output Q_D
);

  wire add_1_c_o, and_1_out;
  wire [3:0] add_1_s, multiplexer_1_out, multiplexer_2_out, multiplexer_3_out;

  PowerSupply powersupply_1 (.VDD(VCC), .GND(GND));
  Add #(.Bits(4)) add_1 (.a({Q_D, Q_C, Q_B, Q_A}), .b(4'b0001), .c_i(1'b0), .s(add_1_s), .c_o(add_1_c_o));
  and and_1 (and_1_out, ENP, ENT);
  Multiplexer #(.Bits(4)) multiplexer_1 (
    .sel(and_1_out), .in_0({Q_D, Q_C, Q_B, Q_A}), .in_1(add_1_s), .out(multiplexer_1_out));
  Multiplexer #(.Bits(4)) multiplexer_2 (
    .sel(nLOAD), .in_0({D, C, B, A}), .in_1(multiplexer_1_out), .out(multiplexer_2_out));
  and and_2 (RC, add_1_c_o, ENT);
  Multiplexer #(.Bits(4)) multiplexer_3 (.sel(nCLR), .in_0(4'b0000), .in_1(multiplexer_2_out), .out(multiplexer_3_out));
  D_FF #(.Bits(4)) Q (.D(multiplexer_3_out), .C(CLK), .Q({Q_D, Q_C, Q_B, Q_A}));  // open: nQ

  // Notes on the sheet:
  //   nCLR: pin 1
  //   CLK: pin 2
  //   nLOAD: pin 9
  //   RC: pin 15
  //   ENT: pin 10
  //   ENP: pin 7
  //   A: pin 3
  //   B: pin 4
  //   C: pin 5
  //   D: pin 6
  //   Q_A: pin 14
  //   Q_B: pin 13
  //   Q_C: pin 12
  //   Q_D: pin 11
  //   VCC: pin 16, default 1
  //   GND: pin 8
  //   CLR	(1)	MR	Master Reset (Active LOW)		Input
  //   CLK	(2)	CP	Clock (Active HIGH Going Edge)	Input
  //   A-D	(3-6)	P0-P3	Parallel			Inputs
  //   ENP	(7)	CEP	Count Enable Parallel		Input
  //   LOAD	(9)	PE	Parallel Enable (Active LOW)	Input
  //   ENT	(10)	CET	Count Enable Trickle		Input
  //   Q_A-Q_D	(11-14)	Q0-Q3	Parallel Outputs		Outputs
  //   RCO	(15)	TC	Terminal Count 		Output
endmodule

/* Test case:
CLK ~CLR ~LOAD ENT ENP   D C B A Q_D Q_C Q_B Q_A

# load
loop(i,4)
loop(n,16)
C  1   0   bits(2,i) bits(4,n)   bits(4,n)
end loop
end loop

# reset
loop(i,8)
loop(n,16)
C  1   0   0   0     bits(4,n)   bits(4,n)
C  0   bits(3,i)     bits(4,n)   bits(4,0)
end loop
end loop

# count
loop(n,16)
C  1   1   1   1     bits(4,0)   bits(4,n+1)
end loop

# hold
loop(n,16)
C  1   0   0   0     bits(4,n)   bits(4,n)
C  1   1   0   0     bits(4,n)   bits(4,n)
C  1   1   1   0     bits(4,n)   bits(4,n)
C  1   1   0   1     bits(4,n)   bits(4,n)
end loop
*/
