// Digital circuit Top.dig as structural Verilog
module Top (
  input  CLK_XTL,
  input  [11:0] LDVALUE,
  input  CLR_SRC,
  input  CLK_SRC,
  input  EPN_SRC,
  input  CLK_pin,
  input  CLR_pin,
  input  LD_SRC,
  input  LD_pin,
  input  EPN_pin
);

  wire _74163_rd_1_rc, _74163_rd_2_rc, CLK, ENP, nCLR, nLD;
  wire [1:0] _74163_rd_3_q_a;
  wire [7:0] _74163_rd_1_q_a;

  Multiplexer multiplexer_1 (.sel(EPN_SRC), .in_0(1'b1), .in_1(EPN_pin), .out(ENP));
  Multiplexer multiplexer_2 (.sel(LD_SRC), .in_0(1'b1), .in_1(LD_pin), .out(nLD));
  Multiplexer multiplexer_3 (.sel(CLK_SRC), .in_0(CLK_XTL), .in_1(CLK_pin), .out(CLK));
  Multiplexer multiplexer_4 (.sel(CLR_SRC), .in_0(1'b1), .in_1(CLR_pin), .out(nCLR));
  _74163_RD _74163_rd_1 (
    .A(LDVALUE[0]), .B(LDVALUE[1]), .C(LDVALUE[2]), .D(LDVALUE[3]), .CLK(CLK), .nCLR(nCLR), .nLOAD(nLD),
    .ENP(ENP), .ENT(1'b1), .Q_A(_74163_rd_1_q_a[0]), .Q_B(_74163_rd_1_q_a[1]), .Q_C(_74163_rd_1_q_a[2]),
    .Q_D(_74163_rd_1_q_a[3]), .RC(_74163_rd_1_rc), .VCC(1'b1), .GND(1'b0));
  _74163_RD _74163_rd_2 (
    .A(LDVALUE[4]), .B(LDVALUE[5]), .C(LDVALUE[6]), .D(LDVALUE[7]), .CLK(CLK), .nCLR(nCLR), .nLOAD(nLD),
    .ENP(ENP), .ENT(_74163_rd_1_rc), .Q_A(_74163_rd_1_q_a[4]), .Q_B(_74163_rd_1_q_a[5]),
    .Q_C(_74163_rd_1_q_a[6]), .Q_D(_74163_rd_1_q_a[7]), .RC(_74163_rd_2_rc), .VCC(1'b1), .GND(1'b0));
  _74163_RD _74163_rd_3 (
    .A(LDVALUE[8]), .B(LDVALUE[9]), .C(LDVALUE[10]), .D(LDVALUE[11]), .CLK(CLK), .nCLR(nCLR), .nLOAD(nLD),
    .ENP(ENP), .ENT(_74163_rd_2_rc), .Q_A(_74163_rd_3_q_a[0]), .Q_B(_74163_rd_3_q_a[1]), .VCC(1'b1),
    .GND(1'b0));  // open: Q_C, Q_D, RC
  // Probe CNT on {_74163_rd_3_q_a, _74163_rd_1_q_a}

  // Notes on the sheet:
  //   CLK_XTL: Hz: 2147483647
endmodule

/* Test case CLK:
              CLK_SRC CLK_XTL CLK_pin CNT    CLR_SRC CLR_pin
# count to 256 using XTL clock
repeat(256)   0       c       0       (n + 1) 0      1

# reset to counter to 0
              0       c       0        x      1      0
# count to 256 using EXT clock
loop(n, 256)
              1       0       0       (n)     1      1
              1       0       1       (n+1)   1      1
end loop
*/

/* Test case CLR:
              CLK_SRC CLK_XTL CLR_SRC CLR_pin EPN_SRC LD_SRC CNT 
              0       0       1       1       0       0      0 
              0       c       1       1       0       0      1
              0       c       1       0       0       0      0
              0       c       1       1       0       0      1
*/

/* Test case EPN:
              CLK_SRC CLK_XTL CLR_SRC EPN_SRC EPN_pin LD_SRC CNT 
              0       0       0       1       1       0      0
              0       c       0       1       1       0      1
              0       c       0       1       0       0      1
              0       c       0       1       1       0      2
*/

/* Test case LD:
              CLK_SRC CLK_XTL LD_SRC LD_pin LDVALUE CNT 
# load a starting value
              0       c       1      0      0xFA    0xFA
*/
